# Fritzing sketch Tempeature Alerting SMS  (saved by Fritzing 0.9.2b)

parts:
  Part1 = Arduino Uno (Rev3)
  T1 = LM35 Temperature Sensor [package="TO92 [THT]"]
  Part2 = Adafruit FONA 3G Breakout [part_number="Adafruit #2691 and #2687"]

nets:
  N1: Part1.A1, T1.Vout
  N2: Part1.D9_PWM, Part2.TXD
  N3: Part1.D10_PWM/SS, Part2.RXD
  GND: Part1.GND, T1.GND, Part2.GND
  N4: Part1.5V, T1.+Vs

custom parts:
  Adafruit FONA 3G Breakout: For those who want to take it to the next level we now have a 3G Cellular Modem breakout! The FONA 3G has better coverage, GSM backwards-compatibility and even sports a built-in GPS module for geolocation & asset tracking. This all-in-one cellular phone module with that lets you add location-tracking, voice, text, SMS and data to your project in a single breakout.
